# Fritzing sketch Schematicfzz (saved by Fritzing 0.9.3b)
breadboards: 1

parts:
  R2 = Resistor [tolerance=±5% resistance=100 package="2010 [SMD]"]
  U3 = RELAY-2 [package=relay-g5v]
  R4 = Resistor [tolerance=±5% resistance=220 package="2010 [SMD]"]
  R3 = Resistor [tolerance=±5% resistance=10k package="2010 [SMD]"]
  VCC1 = 4 x AAA Battery Mount
  U2 = TRANSISTOR_NPN_2 [package=to-92]
  DHT1 = Humidity and Temperature Sensor DHT11
  Esp32 = ESP32S-HiLetgo [part_number=ESP32S-HiLetgo]
  R5 = Resistor [tolerance=±5% resistance=10k package="2010 [SMD]"]
  LED1 = smd LED [color="Red (633nm)" package="0805 [SMD]"]

nets:
  N1: R2.Pin_0, Esp32.GPIO12
  N2: R2.Pin_1, R3.Pin_1, U2.B
  N3: U3.2, U2.C
  N4: U3.9, VCC1.+, Esp32.VIN
  N5: R4.Pin_0, Esp32.GPIO14
  N6: R4.Pin_1, LED1.anode
  GND: R3.Pin_0, VCC1.-, U2.E, DHT1.GND_1, Esp32.GND, LED1.cathode
  N7: DHT1.Vcc, Esp32.3.3, R5.Pin_0
  N8: DHT1.Data-signal, Esp32.GPIO13, R5.Pin_1

custom parts:
  Humidity and Temperature Sensor DHT11: Digital relative humidity & temperature sensor DHT11
  ESP32S-HiLetgo: HiLetgo ESP-WROOM-32 ESP32 ESP-32S Development Board 2.4GHz Dual-Mode WiFi + Bluetooth Dual Cores Microcontroller The ESP32 integrated with Antenna switches, RF Balun, power amplifiers, low-noise amplifiers, filters, and management modules, and the entire solution occupies the least area of PCB. 2.4 GHz Wi-Fi plus Bluetooth dual-mode chip, with TSMC Ultra-low power consumption 40nm technology,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
